# Fritzing sketch pm25-sketch (saved by Fritzing 0.9.2b)
breadboards: 1

parts:
  パーツ1 = Arduino Uno (Rev3)
  RHT1 = Humidity and Temperature Sensor RHT03
  U3 = ESP8266 WiFi Module [part_number=ESP8266]
  R1 = Resistor [tolerance=±5% resistance=330 package="0805 [SMD]"]
  R2 = Resistor [tolerance=±5% resistance=220 package="0805 [SMD]"]
  U1 = LCD-16X2 [package=lcd-16x2_noholes]
  R3 = Resistor [tolerance=±5% resistance=1k package="0805 [SMD]"]
  R4 = Resistor [tolerance=±5% resistance=2.2k package="0805 [SMD]"]
  U4 = GAS_SENSOR [part_number=mq-9 package=mq-3]
  C1 = Capacitor Polarized [part_number=10µF package=cpol-radial-100uf-25v]
  R5 = Resistor [tolerance=±5% resistance=4.7k package=THT]
  U5 = mystery part, 6 pins [chip_label=DN7C3CA006]
  S1 = Pushbutton [package=THT]
  R6 = Resistor [tolerance=±5% resistance=150 package=THT]
  C2 = Electrolytic Capacitor [capacitance=220µF voltage=16V package="100 mil [THT, electrolytic]"]

nets:
  N1: パーツ1.A0, U5.pin2
  N2: パーツ1.A1, U4.A1
  N3: パーツ1.D8, U1.E
  N4: パーツ1.D9_PWM, U1.RS
  N5: パーツ1.D10_PWM/SS, U3.TXD
  N6: パーツ1.D11_PWM/MOSI, R3.Pin_1
  N7: パーツ1.D13/SCK, S1.leg1
  N8: パーツ1.D2, U5.pin4
  N9: パーツ1.D3_PWM, RHT1.Data-signal, R2.Pin_1
  N10: パーツ1.D4, U1.DB7
  N11: パーツ1.D5_PWM, U1.DB6
  N12: パーツ1.D6_PWM, U1.DB5
  N13: パーツ1.D7, U1.DB4
  3V3: パーツ1.3V3, U3.VCC, U3.RST, U3.CH_PD
  5V: パーツ1.5V, RHT1.Vcc, R1.Pin_0, R2.Pin_0, U1.VDD, U4.H2, C1.+, U5.pin1, R6.Pin_0
  GND: パーツ1.GND, RHT1.GND_2, U3.GND, U1.VSS, U1.R_W, U1.K, R4.Pin_0, U4.H1, C1.-, R5.Pin_0, U5.pin3, U5.pin5, S1.leg0, C2.-
  N14: U3.RXD, R3.Pin_0, R4.Pin_1
  N15: R1.Pin_1, U1.A
  N16: U1.VO, R5.Pin_1
  N17: U5.pin6, R6.Pin_1, C2.+

custom parts:
  ESP8266 WiFi Module: Generic WiFi Module based on the ESP8266 with onboard PCB antenna and UART communications
