# Fritzing sketch stripboard (saved by Fritzing 0.9.2b)
perfboards: 2

parts:
  U1 = ESP8266 WiFi Module [part_number=ESP8266]
  LCD1 = LCD screen
  パーツ1 = Arduino Nano (Rev3.0)
  U2 = DN7C3CA006 [chip_label="Place holder for DN7C3CA006" package=THT]
  RHT1 = Humidity and Temperature Sensor RHT03
  R1 = Resistor [tolerance=±5% resistance=2.2k package=THT]
  R2 = Resistor [tolerance=±5% resistance=1k package=THT]  # not connected
  R3 = Resistor [tolerance=±5% resistance=220 package="2512 [SMD]"]
  C1 = Capacitor Polarized [package=panasonic_c]
  U3 = GAS_SENSOR [package=mq-3]
  C3 = Capacitor Polarized [package=panasonic_c]
  R4 = Resistor [tolerance=±5% resistance=150 package=THT]
  R5 = Resistor [tolerance=±5% resistance=330 package="2512 [SMD]"]
  C2 = Capacitor Polarized [package=cpol-radial-100uf-25v]

nets:
  VCC: U1.VCC, U1.RST, U1.CH_PD, パーツ1.3V3
  GND: U1.GND, LCD1.VSS, LCD1.LED-, パーツ1.GND, U2.S-GND, U2.LED-GND, RHT1.GND_2, R1.Pin_1, R3.Pin_1, C1.-, C3.-, C2.-
  N1: U1.TXD, パーツ1.D10
  N2: LCD1.V0, R3.Pin_0
  N3: LCD1.RS, パーツ1.D4
  N4: LCD1.E, パーツ1.D5
  N5: LCD1.DB4, パーツ1.D6
  N6: LCD1.DB5, パーツ1.D7
  N7: LCD1.DB6, パーツ1.D8
  N8: LCD1.DB7, パーツ1.D9
  N9: LCD1.LED+, R5.Pin_1
  N10: パーツ1.D2, RHT1.Data-signal
  N11: パーツ1.D3, U2.LED
  VCC_2: パーツ1.5V, U2.Vcc, RHT1.Vcc, C1.+, U3.H2, R5.Pin_0
  N12: パーツ1.A1, U3.H1
  N13: パーツ1.A0, U2.Vo
  N14: U2.V-LED, C3.+, R4.Pin_1

custom parts:
  ESP8266 WiFi Module: Generic WiFi Module based on the ESP8266 with onboard PCB antenna and UART communications
  DN7C3CA006: A dummy, proxy, ersatz, stand-in part for whatever you want. With 6 pins on a 100 mil inline pin header footprint.
